# Fritzing sketch Climate Controller (saved by Fritzing 0.9.3b)
circuit board: 8.46667cm x 5.64444cm
breadboards: 1

parts:
  Part1 = Adafruit Feather M0 WINC1500 [part_number="Adafruit #3010"]
  Part2 = Adafruit 2.4in TFT FeatherWing [part_number="Adafruit #3315"]  # not connected
  Part3 = Adafruit Radio FeatherWing [part_number="Adafruit #3229, 3230, 3231, 3232"]
  LED1 = RGB LED (com. anode, rbg) [package="5 mm [THT]"]

nets:
  N1: Part1.WAKE, Part3.NC
  N2: Part1.D1, Part3.TX
  N3: Part1.D0, Part3.RX
  N4: Part1.MISO, Part3.MISO
  N5: Part1.MOSI, Part3.MOSI
  N6: Part1.SCK, Part3.SCK
  N7: Part1.A5, Part3.F
  N8: Part1.A4, Part3.M
  N9: Part1.A3, Part3.L, LED1.green_cathode
  N10: Part1.A2, Part3.K, LED1.blue_cathode
  N11: Part1.A1, Part3.J, LED1.red_cathode
  N12: Part1.A0, Part3.I
  GND: Part1.GND, Part3.GND
  N13: Part1.AREF, Part3.AREF
  +3V3: Part1.+3V3, Part3.3.3V, LED1.common_anode
  N14: Part1.!RESET, Part3.RST
  N15: Part1.VBAT, Part3.VBAT
  N16: Part1.EN, Part3.EN
  N17: Part1.VBUS, Part3.USB
  N18: Part1.D13, Part3.H
  N19: Part1.D12, Part3.G
  N20: Part1.D11, Part3.A
  N21: Part1.D10, Part3.B
  N22: Part1.D9, Part3.C
  N23: Part1.D6, Part3.D
  N24: Part1.D5, Part3.E
  N25: Part1.SCL, Part3.SCL
  N26: Part1.SDA, Part3.SDA

custom parts:
  Adafruit Feather M0 WINC1500: This is the Adafruit Feather M0 WiFi w/ATWINC1500 - our take on an 'all-in-one' Arduino-compatible + high speed, reliable WiFi with built in USB and battery charging. Its an Adafruit Feather M0 with a WiFi module, ready to rock! Connect your Feather to the Internet with this fine new FCC-certified WiFi module from Atmel. This 802.11bgn-capable WiFi module is the best new thing for networking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
  Adafruit 2.4in TFT FeatherWing: Spice up your Feather project with a beautiful 2.4" touchscreen display shield with built in microSD card socket. This TFT display is 2.4" diagonal with a bright 4 white-LED backlight. You get 240x320 pixels with individual 16-bit color pixel control. It has way more resolution than a black and white 128x64 display. As a bonus, this display comes with a resistive touchscreen attached to it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
  Adafruit Radio FeatherWing: Add short-hop wireless to your Feather with these Radio Featherwings. These add-ons for any Feather board will let you integrate packetized radio (with the RFM69 radio) or LoRa radio (with the RFM9x's). These radios are good options for kilometer-range radio, and paired with one of our WiFi, cellular or Bluetooth Feathers, will let you bridge from 433/900 MHz to the Internet or your mobile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
